// Logisim project cpu.circ as structural Verilog: 1 circuit, main circuit main
module main (
);

  wire A_IN, A_OUT, AB_SEL0, AB_SEL1, AB_SEL2, ADDR_ABUS_OUT, ADDR_INH, ADDR_INL, ALU_CLC, ALU_IN, ALU_OP,
       ALU_OUT, ALU_SEL0, ALU_SEL1, ALU_SEL2, ALU_STC, and_1_out, and_2_out, and_3_out, and_4_out, and_5_out,
       and_6_out, and_7_out, and_8_out, and_9_out, and_10_out, and_11_out, and_13_out, and_14_out,
       and_15_out, and_16_out, and_17_out, and_18_out, and_21_out, and_22_out, and_23_out, B_IN, B_OUT, C,
       C_IN, C_JMP, C_OUT, CIE, CLK, d_ff_1_q, D_IN, D_OUT, DB_SEL0, DB_SEL1, DB_SEL2, DB_SEL3, DB_SEL4,
       DB_TAR_SEL0, DB_TAR_SEL1, DB_TAR_SEL2, DB_TAR_SEL3, DB_TAR_SEL4, decoder_1_out2, decoder_1_out3,
       decoder_1_out4, decoder_1_out5, decoder_1_out6, decoder_1_out7, decoder_1_out8, decoder_1_out9,
       decoder_1_out10, decoder_2_out0, decoder_2_out1, decoder_2_out2, decoder_2_out3, decoder_3_out0,
       decoder_3_out1, decoder_3_out2, decoder_3_out3, decoder_3_out4, decoder_3_out5, decoder_3_out6,
       decoder_3_out7, DISP_IN, FLAG_INV, FLAGS_IN, FLAGS_OUT, HALT, IDX_ABUS_OUT, IDX_IN, IDX_INH, IDX_INL,
       IDX_OUTH, IDX_OUTL, INSB_HI, INSB_HO, INSB_LI, INSB_LO, IO_OUT, IR2_IN, IR_IN, IRQ, IRQ_OUTH,
       IRQ_OUTL, JMP, MEM_OUT, MISC_SEL0, MISC_SEL1, MISC_SEL2, MISC_SEL3, MODE_out, nor_1_out, nor_2_out,
       not_3_out, not_5_out, OFF_ABUS_OUT, OFF_ABUS_OUT2, OFF_INH, OFF_INL, OFF_OUTH, OFF_OUTL, OP_IN,
       or_1_out, or_2_out, or_3_out, or_4_out, or_5_out, or_6_out, or_8_out, or_9_out, or_10_out, or_11_out,
       or_12_out, or_13_out, or_14_out, or_15_out, or_16_out, or_17_out, or_18_out, OSC_out, PC_ABUS_OUT,
       PC_IN, PC_INC, PC_OUTH, PC_OUTL, PORTA_IN, PORTB_IN, RAM_IN, RESET, RUN, RUN_STOP_out, S, S_JMP, SIE,
       SP_ABUS_OUT, SP_DEC, SP_INC, STEP_out, t_ff_1_q, T_ONE, T_RESET, T_ZERO, xor_1_out, xor_2_out,
       xor_3_out, Z, Z_JMP;
  wire [1:0] MODE, rom_2_p1;
  wire [2:0] pull_resistor_4_node;
  wire [3:0] INSTA_I, INSTA_O, T_STATE, undriven_4, undriven_6, undriven_8, undriven_10;
  wire [3:2] _4x28C16_data_2;
  wire [3:3] _4x28C16_data;
  wire [5:0] U_out;
  wire [7:0] adder_1_out, and_20_out, controlled_buffer_25_out, counter_5_q, counter_7_q, counter_7_q_2,
       divider_1_rem, IR_REG, IR_REG2, multiplexer_1_out, multiplier_1_cout, multiplier_1_out, not_6_out,
       not_6_out_2, OP_REG, register_1_q, register_1_q_2, register_2_q, register_6_q, register_7_q,
       register_8_q, register_9_q, register_10_q, register_11_q, register_14_q, register_15_q, register_16_q,
       register_17_q, register_18_q, register_19_q, register_20_q, register_21_q, rom_1_data,
       subtractor_1_out, W_BUS, xor_4_out;
  wire [7:4] undriven_5, undriven_7, undriven_9, undriven_11;
  wire [8:0] shifter_1_out, undriven, undriven_2, undriven_3;
  wire [8:8] adder_1_cout, and_19_out, multiplexer_1_out_2, subtractor_1_bout;
  wire [10:10] controlled_buffer_23_out;
  wire [14:0] controlled_buffer_32_out, counter_6_q, not_7_out, register_22_q;
  wire [15:0] AD_BUS, controlled_buffer_11_out, controlled_buffer_37_out, counter_1_q, not_4_out,
       subtractor_2_out;
  wire [15:15] not_1_out, not_2_out;

  LED Df (.in(register_1_q[7]));
  LED Df_2 (.in(AD_BUS[15]));
  assign W_BUS = IRQ_OUTL ? {8{1'b1}} : 8'bz;  // Controlled_Buffer controlled_buffer_1
  LED De (.in(register_1_q[6]));
  LED Dd (.in(register_1_q[5]));
  LED Dc (.in(register_1_q[4]));
  LED Db (.in(register_1_q[3]));
  assign AD_BUS = ADDR_ABUS_OUT ? {register_1_q, register_1_q_2} : 16'bz;  // Controlled_Buffer controlled_buffer_2
  LED De_2 (.in(AD_BUS[14]));
  LED Dd_2 (.in(AD_BUS[13]));
  LED Dc_2 (.in(AD_BUS[12]));
  LED Db_2 (.in(AD_BUS[11]));
  Pull_Resistor pull_resistor_1 (.node(AD_BUS));
  assign W_BUS = FLAGS_OUT ? {{5{1'b0}}, S, Z, C} : 8'bz;  // Controlled_Buffer controlled_buffer_3
  Button U (.out(U_out[0]));
  Button L (.out(U_out[1]));
  Button D (.out(U_out[5]));
  LED Da (.in(register_1_q[2]));
  LED D9 (.in(register_1_q[1]));
  LED D8 (.in(register_1_q[0]));
  LED Da_2 (.in(AD_BUS[10]));
  LED D9_2 (.in(AD_BUS[9]));
  LED D8_2 (.in(AD_BUS[8]));
  LED D7 (.in(AD_BUS[7]));
  assign W_BUS = IRQ_OUTH ? 8'hfe : 8'bz;  // Controlled_Buffer controlled_buffer_4
  and and_1 (and_1_out, ~INSB_HI, ~INSB_LI);  // AND_Gate
  assign {DB_TAR_SEL3, DB_TAR_SEL2, DB_TAR_SEL1, DB_TAR_SEL0} = and_1_out ? INSTA_I : 4'bz;  // Controlled_Buffer controlled_buffer_5
  assign {DB_TAR_SEL3, DB_TAR_SEL2, DB_TAR_SEL1, DB_TAR_SEL0} = INSB_LI ? IR_REG2[3:0] : 4'bz;  // Controlled_Buffer controlled_buffer_6
  assign {DB_TAR_SEL3, DB_TAR_SEL2, DB_TAR_SEL1, DB_TAR_SEL0} = INSB_HI ? IR_REG2[7:4] : 4'bz;  // Controlled_Buffer controlled_buffer_7
  assign {DB_SEL3, DB_SEL2, DB_SEL1, DB_SEL0} = INSB_LO ? IR_REG2[3:0] : 4'bz;  // Controlled_Buffer controlled_buffer_8
  assign {DB_SEL3, DB_SEL2, DB_SEL1, DB_SEL0} = INSB_HO ? IR_REG2[7:4] : 4'bz;  // Controlled_Buffer controlled_buffer_9
  assign {DB_SEL3, DB_SEL2, DB_SEL1, DB_SEL0} = and_2_out ? INSTA_O : 4'bz;  // Controlled_Buffer controlled_buffer_10
  and and_2 (and_2_out, ~INSB_HO, ~INSB_LO);  // AND_Gate
  Button R (.out(U_out[2]));
  LED D7_2 (.in(register_1_q_2[7]));
  LED D6 (.in(register_1_q_2[6]));
  LED D5 (.in(register_1_q_2[5]));
  LED D4 (.in(register_1_q_2[4]));
  assign controlled_buffer_11_out = ADDR_INL ? {register_1_q, W_BUS} : 16'bz;  // Controlled_Buffer controlled_buffer_11
  assign controlled_buffer_11_out = ADDR_INH ? {W_BUS, register_1_q_2} : 16'bz;  // Controlled_Buffer controlled_buffer_12
  LED D6_2 (.in(AD_BUS[6]));
  LED D5_2 (.in(AD_BUS[5]));
  LED D4_2 (.in(AD_BUS[4]));
  LED D3 (.in(AD_BUS[3]));
  LED D7_3 (.in(W_BUS[7]));
  LED D6_3 (.in(W_BUS[6]));
  Pull_Resistor pull_resistor_2 (.node(W_BUS));
  Button B (.out(U_out[3]));
  Button A (.out(U_out[4]));
  LED D3_2 (.in(register_1_q_2[3]));
  LED D2 (.in(register_1_q_2[2]));
  LED D1 (.in(register_1_q_2[1]));
  LED D0 (.in(register_1_q_2[0]));
  or or_1 (or_1_out, ADDR_INH, ADDR_INL);
  LED D2_2 (.in(AD_BUS[2]));
  LED D1_2 (.in(AD_BUS[1]));
  LED D0_2 (.in(AD_BUS[0]));
  LED D5_3 (.in(W_BUS[5]));
  LED D4_3 (.in(W_BUS[4]));
  LED D3_3 (.in(W_BUS[3]));
  LED D2_3 (.in(W_BUS[2]));
  assign W_BUS = IRQ ? 8'h7f : 8'bz;  // Controlled_Buffer controlled_buffer_13
  or or_2 (or_2_out, U_out[0], U_out[5], U_out[4], U_out[3], U_out[2], U_out[1]);
  Register #(.width(16)) register_1 (
    .D(controlled_buffer_11_out), .en(or_1_out), .Q({register_1_q, register_1_q_2}), .clk(CLK), .clr(RESET));
  LED D1_3 (.in(W_BUS[1]));
  LED D0_3 (.in(W_BUS[0]));
  assign W_BUS = IO_OUT ? register_2_q : 8'bz;  // Controlled_Buffer controlled_buffer_14
  Register register_2 (.D({2'b00, U_out}), .Q(register_2_q), .clk(or_2_out));  // open: en, clr
  not not_1 (not_1_out[15], AD_BUS[15]);
  and and_3 (and_3_out, PC_INC, ~IRQ);  // AND_Gate
  Button u_RESET (.out(RESET));
  Button RUN_STOP (.out(RUN_STOP_out));
  T_Flip_Flop #(.enable("true")) t_ff_1 (
    .clk(or_2_out), .T(1'b1), .Q(t_ff_1_q), .reset(or_3_out), .en(1'b1));  // open: Qn, preset
  or or_3 (or_3_out, and_6_out, RESET);
  D_Flip_Flop d_ff_1 (.D(1'b1), .Q(d_ff_1_q), .preset(SIE), .reset(or_4_out));  // open: clk, Qn
  or or_4 (or_4_out, CIE, RESET);
  LED D7_4 (.in(not_2_out[15]));
  LED D6_4 (.in(counter_1_q[14]));
  assign AD_BUS = PC_ABUS_OUT ? {not_2_out[15], counter_1_q[14:0]} : 16'bz;  // Controlled_Buffer controlled_buffer_15
  Counter #(.max('hffff), .width(16)) counter_1 (
    .load(JMP), .D({not_1_out[15], AD_BUS[14:0]}), .count(and_3_out), .Q(counter_1_q), .clk(CLK), .clr(RESET));  // open: carry
  T_Flip_Flop #(.enable("true")) t_ff_2 (
    .clk(RUN_STOP_out), .T(1'b1), .Q(RUN), .reset(RESET), .en(1'b1));  // open: Qn, preset
  and and_4 (and_4_out, MEM_OUT, ~AD_BUS[15]);  // AND_Gate
  RAM #(.addrWidth(15), .databus("bidir")) ram_1 (.addr(AD_BUS[14:0]), .data(W_BUS));  // open: we, oe, clk
  ROM #(.addrWidth(15)) rom_1 (.addr(AD_BUS[14:0]), .data(rom_1_data));
  and and_5 (and_5_out, T_RESET, t_ff_1_q, d_ff_1_q);
  and and_6 (and_6_out, IRQ, T_ONE);
  LED D5_4 (.in(counter_1_q[13]));
  LED D4_4 (.in(counter_1_q[12]));
  LED D3_4 (.in(counter_1_q[11]));
  LED D2_4 (.in(counter_1_q[10]));
  not not_2 (not_2_out[15], counter_1_q[15]);
  Button STEP (.out(STEP_out));
  Clock OSC (.out(OSC_out));
  nor nor_1 (nor_1_out, C_JMP, Z_JMP, S_JMP);
  xor xor_1 (xor_1_out, C, FLAG_INV);
  xor xor_2 (xor_2_out, Z, FLAG_INV);
  xor xor_3 (xor_3_out, S, FLAG_INV);
  D_Flip_Flop d_ff_2 (.D(and_5_out), .Q(IRQ), .preset(and_5_out), .reset(or_5_out));  // open: clk, Qn
  or or_5 (or_5_out, T_ONE, RESET);
  LED D1_4 (.in(counter_1_q[9]));
  LED D0_4 (.in(counter_1_q[8]));
  LED D7_5 (.in(counter_1_q[7]));
  Counter #(.max('hffff), .width(16)) counter_2 (.count(CLK), .clk(CLK), .clr(RESET));  // open: load, D, Q, carry
  and and_7 (and_7_out, STEP_out, ~RUN);  // AND_Gate
  and and_8 (and_8_out, RUN, OSC_out);
  and and_9 (and_9_out, C_JMP, xor_1_out);
  and and_10 (and_10_out, Z_JMP, xor_2_out);
  and and_11 (and_11_out, S_JMP, xor_3_out);
  LED D6_5 (.in(counter_1_q[6]));
  LED D5_5 (.in(counter_1_q[5]));
  LED D4_5 (.in(counter_1_q[4]));
  LED D3_5 (.in(counter_1_q[3]));
  assign W_BUS = PC_OUTH ? counter_1_q[7:0] : 8'bz;  // Controlled_Buffer controlled_buffer_16
  assign W_BUS = PC_OUTL ? {not_2_out[15], counter_1_q[14:8]} : 8'bz;  // Controlled_Buffer controlled_buffer_17
  or or_6 (or_6_out, and_7_out, and_8_out);
  and and_12 (CLK, or_6_out, ~HALT);  // AND_Gate
  and and_13 (and_13_out, PC_IN, nor_1_out);
  and and_14 (and_14_out, PC_IN, and_9_out);
  and and_15 (and_15_out, PC_IN, and_10_out);
  and and_16 (and_16_out, PC_IN, and_11_out);
  and and_17 (and_17_out, ~IRQ, AD_BUS[15], MEM_OUT);  // AND_Gate
  assign W_BUS = and_17_out ? rom_1_data : 8'bz;  // Controlled_Buffer controlled_buffer_18
  LED D0_5 (.in(counter_1_q[0]));
  LED D2_5 (.in(counter_1_q[2]));
  LED D1_5 (.in(counter_1_q[1]));
  or or_7 (JMP, and_13_out, and_14_out, and_15_out, and_16_out);
  or or_8 (or_8_out, and_18_out, T_ZERO);
  assign W_BUS = A_OUT ? register_6_q : 8'bz;  // Controlled_Buffer controlled_buffer_19
  assign W_BUS = B_OUT ? register_7_q : 8'bz;  // Controlled_Buffer controlled_buffer_20
  assign W_BUS = C_OUT ? register_8_q : 8'bz;  // Controlled_Buffer controlled_buffer_21
  assign W_BUS = D_OUT ? register_9_q : 8'bz;  // Controlled_Buffer controlled_buffer_22
  assign controlled_buffer_23_out[10] = or_8_out ? T_STATE[3] : 1'bz;  // Controlled_Buffer controlled_buffer_23
  assign controlled_buffer_23_out[10] = not_3_out ? IR_REG[7] : 1'bz;  // Controlled_Buffer controlled_buffer_24
  not not_3 (not_3_out, or_8_out);
  and and_18 (and_18_out, IR_REG[6], IR_REG[5], IR_REG[4]);
  Counter #(.max('hf), .width(4)) counter_3 (
    .count(CLK), .Q(T_STATE), .clk(CLK), .clr(or_9_out));  // open: load, D, carry
  or or_9 (or_9_out, T_RESET, RESET);
  Register register_3 (.D(W_BUS), .en(IR_IN), .Q(IR_REG), .clk(CLK), .clr(RESET));
  Register register_4 (.D(W_BUS), .en(IR2_IN), .Q(IR_REG2), .clk(CLK), .clr(RESET));
  Register register_5 (.D(W_BUS), .en(OP_IN), .Q(OP_REG), .clk(CLK), .clr(RESET));
  Register register_6 (.D(W_BUS), .en(A_IN), .Q(register_6_q), .clk(CLK), .clr(RESET));
  Register register_7 (.D(W_BUS), .en(B_IN), .Q(register_7_q), .clk(CLK), .clr(RESET));
  Register register_8 (.D(W_BUS), .en(C_IN), .Q(register_8_q), .clk(CLK), .clr(RESET));
  Register register_9 (.D(W_BUS), .en(D_IN), .Q(register_9_q), .clk(CLK), .clr(RESET));
  ROM #(.addrWidth(11), .dataWidth(32)) _4x28C16 (
    .addr({controlled_buffer_23_out[10], IR_REG[6:0], T_STATE[2:0]}),
    .data({_4x28C16_data_2, PC_IN, IDX_IN, MISC_SEL3, MISC_SEL2, MISC_SEL1, MISC_SEL0, INSB_HO, INSB_HI, INSB_LO, INSB_LI, _4x28C16_data[3], S_JMP, Z_JMP, C_JMP, ALU_SEL2, ALU_SEL1, ALU_SEL0, DB_SEL4, INSTA_O, AB_SEL2, AB_SEL1, AB_SEL0, DB_TAR_SEL4, INSTA_I}));
  LED T0 (.in(T_ZERO));
  LED T1 (.in(T_ONE));
  LED T2 (.in(decoder_1_out2));
  LED T3 (.in(decoder_1_out3));
  Decoder #(.select(4)) decoder_1 (
    .out0(T_ZERO), .out1(T_ONE), .out2(decoder_1_out2), .out3(decoder_1_out3), .out4(decoder_1_out4),
    .out5(decoder_1_out5), .out6(decoder_1_out6), .out7(decoder_1_out7), .out8(decoder_1_out8),
    .out9(decoder_1_out9), .out10(decoder_1_out10), .sel(T_STATE));  // open: out11, out12, out13, out14, out15, en
  LED D7_6 (.in(IR_REG[7]));
  LED D6_6 (.in(IR_REG[6]));
  LED D5_6 (.in(IR_REG[5]));
  LED D4_6 (.in(IR_REG[4]));
  LED D7_7 (.in(IR_REG2[7]));
  LED D6_7 (.in(IR_REG2[6]));
  LED D5_7 (.in(IR_REG2[5]));
  LED D4_7 (.in(IR_REG2[4]));
  LED D7_8 (.in(OP_REG[7]));
  LED D6_8 (.in(OP_REG[6]));
  LED D5_8 (.in(OP_REG[5]));
  LED D4_8 (.in(OP_REG[4]));
  LED D7_9 (.in(register_6_q[7]));
  LED D6_9 (.in(register_6_q[6]));
  LED D5_9 (.in(register_6_q[5]));
  LED D4_9 (.in(register_6_q[4]));
  LED D7_10 (.in(register_7_q[7]));
  LED D6_10 (.in(register_7_q[6]));
  LED D5_10 (.in(register_7_q[5]));
  LED D4_10 (.in(register_7_q[4]));
  LED D7_11 (.in(register_8_q[7]));
  LED D6_11 (.in(register_8_q[6]));
  LED D5_11 (.in(register_8_q[5]));
  LED D4_11 (.in(register_8_q[4]));
  LED D7_12 (.in(register_9_q[7]));
  LED D6_12 (.in(register_9_q[6]));
  LED D5_12 (.in(register_9_q[5]));
  LED D4_12 (.in(register_9_q[4]));
  LED T4 (.in(decoder_1_out4));
  LED T5 (.in(decoder_1_out5));
  LED T6 (.in(decoder_1_out6));
  LED T7 (.in(decoder_1_out7));
  LED D3_6 (.in(IR_REG[3]));
  LED D2_6 (.in(IR_REG[2]));
  LED D1_6 (.in(IR_REG[1]));
  LED D0_6 (.in(IR_REG[0]));
  LED D3_7 (.in(IR_REG2[3]));
  LED D2_7 (.in(IR_REG2[2]));
  LED D1_7 (.in(IR_REG2[1]));
  LED D0_7 (.in(IR_REG2[0]));
  LED D3_8 (.in(OP_REG[3]));
  LED D2_8 (.in(OP_REG[2]));
  LED D1_8 (.in(OP_REG[1]));
  LED D0_8 (.in(OP_REG[0]));
  LED D3_9 (.in(register_6_q[3]));
  LED D2_9 (.in(register_6_q[2]));
  LED D1_9 (.in(register_6_q[1]));
  LED D0_9 (.in(register_6_q[0]));
  LED D3_10 (.in(register_7_q[3]));
  LED D2_10 (.in(register_7_q[2]));
  LED D1_10 (.in(register_7_q[1]));
  LED D0_10 (.in(register_7_q[0]));
  LED D3_11 (.in(register_8_q[3]));
  LED D2_11 (.in(register_8_q[2]));
  LED D1_11 (.in(register_8_q[1]));
  LED D0_11 (.in(register_8_q[0]));
  LED D3_12 (.in(register_9_q[3]));
  LED D2_12 (.in(register_9_q[2]));
  LED D1_12 (.in(register_9_q[1]));
  LED D0_12 (.in(register_9_q[0]));
  LED T8 (.in(decoder_1_out8));
  LED T9 (.in(decoder_1_out9));
  LED TA (.in(decoder_1_out10));
  LED TB ();  // open: in
  LED TC ();  // open: in
  LED TD ();  // open: in
  LED TE ();  // open: in
  LED TF ();  // open: in
  or or_10 (or_10_out, ALU_IN, ALU_OP);
  assign controlled_buffer_25_out = ALU_IN ? W_BUS : 8'bz;  // Controlled_Buffer controlled_buffer_25
  and and_19 (and_19_out[8], C, C_JMP);
  Pull_Resistor pull_resistor_3 (.node(OP_REG));
  Decoder #(.select(2)) decoder_2 (
    .out0(decoder_2_out0), .out1(decoder_2_out1), .out2(decoder_2_out2), .out3(decoder_2_out3), .sel(MODE));  // open: en
  assign W_BUS = ALU_OUT ? register_10_q : 8'bz;  // Controlled_Buffer controlled_buffer_26
  Register register_10 (.D(controlled_buffer_25_out), .en(or_10_out), .Q(register_10_q), .clk(CLK), .clr(RESET));
  D_Flip_Flop #(.enable("true")) d_ff_3 (
    .clk(CLK), .D(or_12_out), .Q(C), .preset(ALU_STC), .en(or_13_out), .reset(or_11_out));  // open: Qn
  or or_11 (or_11_out, RESET, ALU_CLC);
  Adder adder_1 (.a(OP_REG), .b(W_BUS), .out(adder_1_out), .cin(and_19_out[8]), .cout(adder_1_cout[8]));
  Subtractor subtractor_1 (
    .a(W_BUS), .b(OP_REG), .out(subtractor_1_out), .bin(and_19_out[8]), .bout(subtractor_1_bout[8]));
  assign xor_4_out = OP_REG ^ W_BUS;  // XOR_Gate xor_4, 8 bits wide
  assign and_20_out = OP_REG & W_BUS;  // AND_Gate and_20, 8 bits wide
  Divider divider_1 (.a(OP_REG), .b(W_BUS), .rem(divider_1_rem));  // open: out, upper
  Multiplier multiplier_1 (.a(OP_REG), .b(W_BUS), .out(multiplier_1_out), .cout(multiplier_1_cout));  // open: cin
  Pull_Resistor pull_resistor_4 (.node(pull_resistor_4_node));
  Counter #(.max('h3), .width(2)) counter_4 (.D(rom_2_p1), .Q(MODE), .clk(MODE_out));  // open: load, count, carry, clr
  Register register_11 (.D(W_BUS), .en(DISP_IN), .Q(register_11_q), .clk(CLK), .clr(RESET));
  Button u_MODE (.out(MODE_out));
  LED UNSINGED (.in(decoder_2_out0));
  LED SIGNED (.in(decoder_2_out1));
  LED HEX (.in(decoder_2_out2));
  LED OCTAL (.in(decoder_2_out3));
  LED D7_13 (.in(register_10_q[7]));
  LED D6_13 (.in(register_10_q[6]));
  LED D5_13 (.in(register_10_q[5]));
  LED D4_13 (.in(register_10_q[4]));
  assign controlled_buffer_25_out = ALU_OP ? multiplexer_1_out : 8'bz;  // Controlled_Buffer controlled_buffer_27
  Shifter #(.shift("rr"), .width(9)) shifter_1 (
    .in({and_19_out[8], W_BUS}), .\dist ({pull_resistor_4_node, 1'b1}), .out(shifter_1_out));
  Decoder #(.select(4)) decoder_3 (
    .out0(decoder_3_out0), .out1(decoder_3_out1), .out2(decoder_3_out2), .out3(decoder_3_out3),
    .out4(decoder_3_out4), .out5(decoder_3_out5), .out6(decoder_3_out6), .out7(decoder_3_out7),
    .sel(counter_5_q[3:0]), .en(PORTB_IN));  // open: out8, out9, out10, out11, out12, out13, out14, out15
  Counter counter_5 (.load(PORTA_IN), .D(W_BUS), .count(PORTA_IN), .Q(counter_5_q), .clk(CLK));  // open: carry, clr
  // ROM #(.addrWidth(10), .dataWidth(32)) rom_2: pin names not known; wires that end beside it: rom_2_p1, DISP_IN, {MODE, register_11_q}
  _7_Segment_Display u_7_segment_display_1 (
    .g(undriven_11[7]), .f(undriven_11[6]), .a(undriven_11[5]), .b(undriven_11[4]), .e(undriven_10[3]),
    .d(undriven_10[2]), .c(undriven_10[1]), .dp(undriven_10[0]));
  LED D3_13 (.in(register_10_q[3]));
  LED D2_13 (.in(register_10_q[2]));
  LED D1_13 (.in(register_10_q[1]));
  LED D0_13 (.in(register_10_q[0]));
  Register #(.width(1)) register_12 (.D(or_14_out), .en(or_13_out), .Q(Z), .clk(CLK), .clr(RESET));
  Multiplexer #(.enable("false"), .select(3), .width(9)) multiplexer_1 (
    .in0({adder_1_cout[8], adder_1_out}), .in1({subtractor_1_bout[8], subtractor_1_out}),
    .in2({1'b0, xor_4_out}), .in3({1'b0, and_20_out}), .in4(undriven), .in5(undriven_2), .in6(shifter_1_out),
    .in7(undriven_3), .out({multiplexer_1_out_2[8], multiplexer_1_out}), .sel({ALU_SEL2, ALU_SEL1, ALU_SEL0}));
  _7_Segment_Display u_7_segment_display_2 (
    .g(undriven_9[7]), .f(undriven_9[6]), .a(undriven_9[5]), .b(undriven_9[4]), .e(undriven_8[3]),
    .d(undriven_8[2]), .c(undriven_8[1]), .dp(undriven_8[0]));
  _7_Segment_Display u_7_segment_display_3 (
    .g(undriven_7[7]), .f(undriven_7[6]), .a(undriven_7[5]), .b(undriven_7[4]), .e(undriven_6[3]),
    .d(undriven_6[2]), .c(undriven_6[1]), .dp(undriven_6[0]));
  LED u_C (.in(C));
  LED u_Z (.in(Z));
  LED u_S (.in(S));
  Register #(.width(1)) register_13 (.D(or_15_out), .en(or_13_out), .Q(S), .clk(CLK), .clr(RESET));
  or or_12 (or_12_out, multiplexer_1_out_2[8], and_21_out);
  and and_21 (and_21_out, W_BUS[0], FLAGS_IN);
  nor nor_2 (nor_2_out, multiplexer_1_out[3], multiplexer_1_out[2], multiplexer_1_out[1], multiplexer_1_out[0], multiplexer_1_out[7], multiplexer_1_out[6], multiplexer_1_out[5], multiplexer_1_out[4]);
  Register register_14 (.D(W_BUS), .en(decoder_3_out0), .Q(register_14_q), .clk(CLK));  // open: clr
  Register register_15 (.D(W_BUS), .en(decoder_3_out2), .Q(register_15_q), .clk(CLK));  // open: clr
  Register register_16 (.D(W_BUS), .en(decoder_3_out4), .Q(register_16_q), .clk(CLK));  // open: clr
  Register register_17 (.D(W_BUS), .en(decoder_3_out6), .Q(register_17_q), .clk(CLK));  // open: clr
  _7_Segment_Display u_7_segment_display_4 (
    .g(undriven_5[7]), .f(undriven_5[6]), .a(undriven_5[5]), .b(undriven_5[4]), .e(undriven_4[3]),
    .d(undriven_4[2]), .c(undriven_4[1]), .dp(undriven_4[0]));
  or or_13 (or_13_out, FLAGS_IN, ALU_OP);
  or or_14 (or_14_out, nor_2_out, and_22_out);
  or or_15 (or_15_out, multiplexer_1_out[7], and_23_out);
  and and_22 (and_22_out, W_BUS[1], FLAGS_IN);
  Register register_18 (.D(W_BUS), .en(decoder_3_out1), .Q(register_18_q), .clk(CLK));  // open: clr
  Register register_19 (.D(W_BUS), .en(decoder_3_out3), .Q(register_19_q), .clk(CLK));  // open: clr
  Register register_20 (.D(W_BUS), .en(decoder_3_out5), .Q(register_20_q), .clk(CLK));  // open: clr
  Register register_21 (.D(W_BUS), .en(decoder_3_out7), .Q(register_21_q), .clk(CLK));  // open: clr
  and and_23 (and_23_out, W_BUS[2], FLAGS_IN);
  DotMatrix #(.dotshape("circle"), .inputtype("row"), .matrixcols(8), .matrixrows(8)) dotmatrix_1 (
    .row0(register_14_q), .row1(register_18_q), .row2(register_15_q), .row3(register_19_q),
    .row4(register_16_q), .row5(register_20_q), .row6(register_17_q), .row7(register_21_q));
  LED Df_3 (.in(not_6_out[7]));
  LED De_3 (.in(not_6_out[6]));
  assign AD_BUS = IDX_ABUS_OUT ? {not_6_out, not_6_out_2} : 16'bz;  // Controlled_Buffer controlled_buffer_28
  assign W_BUS = IDX_OUTH ? not_6_out_2 : 8'bz;  // Controlled_Buffer controlled_buffer_29
  Decoder #(.enable("false"), .select(4)) decoder_4 (
    .out1(CIE), .out2(SIE), .out3(T_RESET), .out4(HALT), .out5(SP_INC), .out6(SP_DEC), .out7(FLAG_INV),
    .out8(ALU_STC), .out9(ALU_CLC), .out10(PC_INC), .sel({MISC_SEL3, MISC_SEL2, MISC_SEL1, MISC_SEL0}));  // open: out0, out11, out12, out13, out14, out15
  Decoder #(.enable("false"), .select(5)) decoder_5 (
    .out1(A_OUT), .out2(B_OUT), .out3(C_OUT), .out4(D_OUT), .out5(OFF_OUTH), .out6(OFF_OUTL), .out7(ALU_OUT),
    .out8(FLAGS_OUT), .out9(IRQ_OUTL), .out10(IRQ_OUTH), .out11(PC_OUTL), .out12(PC_OUTH), .out13(IDX_OUTL),
    .out14(IDX_OUTH), .out15(MEM_OUT), .out16(IO_OUT), .sel({DB_SEL4, DB_SEL3, DB_SEL2, DB_SEL1, DB_SEL0}));  // open: out0, out17, out18, out19, out20, out21, out22, out23, out24, out25, out26, out27, out28, out29, out30, out31
  LED Dd_3 (.in(not_6_out[5]));
  LED Dc_3 (.in(not_6_out[4]));
  LED Db_3 (.in(not_6_out[3]));
  LED Da_3 (.in(not_6_out[2]));
  assign W_BUS = IDX_OUTL ? not_6_out : 8'bz;  // Controlled_Buffer controlled_buffer_30
  LED E (.in(not_7_out[14]));
  LED D_2 (.in(not_7_out[13]));
  assign AD_BUS = SP_ABUS_OUT ? {1'b0, not_7_out} : 16'bz;  // Controlled_Buffer controlled_buffer_31
  LED D9_3 (.in(not_6_out[1]));
  LED D8_3 (.in(not_6_out[0]));
  LED D7_14 (.in(not_6_out_2[7]));
  LED D6_14 (.in(not_6_out_2[6]));
  LED C_2 (.in(not_7_out[12]));
  LED B_2 (.in(not_7_out[11]));
  LED A_2 (.in(not_7_out[10]));
  LED _9 (.in(not_7_out[9]));
  LED D5_14 (.in(not_6_out_2[5]));
  LED D4_14 (.in(not_6_out_2[4]));
  LED D3_14 (.in(not_6_out_2[3]));
  LED D2_14 (.in(not_6_out_2[2]));
  assign not_4_out[14:0] = ~controlled_buffer_32_out;  // NOT_Gate not_4, 15 bits wide
  assign {not_4_out[15], controlled_buffer_32_out} = IDX_INL ? {not_6_out, W_BUS} : 16'bz;  // Controlled_Buffer controlled_buffer_32
  assign {not_4_out[15], controlled_buffer_32_out} = IDX_IN ? AD_BUS : 16'bz;  // Controlled_Buffer controlled_buffer_33
  assign {not_4_out[15], controlled_buffer_32_out} = IDX_INH ? {W_BUS, not_6_out_2} : 16'bz;  // Controlled_Buffer controlled_buffer_34
  Pull_Resistor pull_resistor_5 (.node({not_4_out[15], controlled_buffer_32_out}));
  or or_16 (or_16_out, IDX_INH, IDX_IN, IDX_INL);
  LED _8 (.in(not_7_out[8]));
  LED _7 (.in(not_7_out[7]));
  LED _6 (.in(not_7_out[6]));
  not not_5 (not_5_out, SP_INC);
  or or_17 (or_17_out, SP_INC, SP_DEC);
  LED D1_14 (.in(not_6_out_2[1]));
  LED D0_14 (.in(not_6_out_2[0]));
  Register #(.width(16)) register_22 (
    .D(not_4_out), .en(or_16_out), .Q({not_6_out[7], register_22_q}), .clk(CLK), .clr(RESET));
  LED _5 (.in(not_7_out[5]));
  LED _4 (.in(not_7_out[4]));
  LED _3 (.in(not_7_out[3]));
  LED _2 (.in(not_7_out[2]));
  Counter #(.max('h7fff), .width(15)) counter_6 (
    .load(1'b0), .count(or_17_out), .Q(counter_6_q), .up(not_5_out), .clk(CLK), .clr(RESET));  // open: D, carry
  assign {not_6_out[6:0], not_6_out_2} = ~register_22_q;  // NOT_Gate not_6, 15 bits wide
  LED _1 (.in(not_7_out[1]));
  LED _0 (.in(not_7_out[0]));
  assign not_7_out = ~counter_6_q;  // NOT_Gate not_7, 15 bits wide
  Decoder #(.enable("false"), .select(3)) decoder_6 (
    .out1(SP_ABUS_OUT), .out2(ADDR_ABUS_OUT), .out3(PC_ABUS_OUT), .out4(IDX_ABUS_OUT), .out5(OFF_ABUS_OUT),
    .out6(OFF_ABUS_OUT2), .sel({AB_SEL2, AB_SEL1, AB_SEL0}));  // open: out0, out7
  LED Df_4 (.in(counter_7_q[7]));
  LED De_4 (.in(counter_7_q[6]));
  LED Dd_4 (.in(counter_7_q[5]));
  LED Dc_4 (.in(counter_7_q[4]));
  assign AD_BUS = OFF_ABUS_OUT2 ? {counter_7_q, counter_7_q_2} : 16'bz;  // Controlled_Buffer controlled_buffer_35
  Subtractor #(.width(16)) subtractor_2 (
    .a({not_6_out, not_6_out_2}), .b({counter_7_q, counter_7_q_2}), .out(subtractor_2_out));  // open: bin, bout
  assign AD_BUS = OFF_ABUS_OUT ? subtractor_2_out : 16'bz;  // Controlled_Buffer controlled_buffer_36
  Hex_Digit_Display hex_digit_display_1 (.value({1'b0, not_7_out[14:12]}));  // open: dp
  Hex_Digit_Display hex_digit_display_2 (.value(not_7_out[11:8]));  // open: dp
  Decoder #(.enable("false"), .select(5)) decoder_7 (
    .out1(A_IN), .out2(B_IN), .out3(C_IN), .out4(D_IN), .out5(OFF_INH), .out6(OFF_INL), .out7(RAM_IN),
    .out8(DISP_IN), .out9(IR_IN), .out10(IR2_IN), .out11(ALU_OP), .out12(FLAGS_IN), .out13(ALU_IN),
    .out14(IDX_INL), .out15(IDX_INH), .out16(PORTA_IN), .out17(PORTB_IN), .out18(ADDR_INH), .out19(ADDR_INL),
    .out20(OP_IN), .sel({DB_TAR_SEL4, DB_TAR_SEL3, DB_TAR_SEL2, DB_TAR_SEL1, DB_TAR_SEL0}));  // open: out0, out21, out22, out23, out24, out25, out26, out27, out28, out29, out30, out31
  LED Db_4 (.in(counter_7_q[3]));
  LED Da_4 (.in(counter_7_q[2]));
  LED D9_4 (.in(counter_7_q[1]));
  LED D8_4 (.in(counter_7_q[0]));
  Hex_Digit_Display hex_digit_display_3 (.value(not_7_out[7:4]));  // open: dp
  Hex_Digit_Display hex_digit_display_4 (.value(not_7_out[3:0]));  // open: dp
  LED D7_15 (.in(counter_7_q_2[7]));
  LED D6_15 (.in(counter_7_q_2[6]));
  LED D5_15 (.in(counter_7_q_2[5]));
  LED D4_15 (.in(counter_7_q_2[4]));
  LED D3_15 (.in(counter_7_q_2[3]));
  LED D2_15 (.in(counter_7_q_2[2]));
  LED D1_15 (.in(counter_7_q_2[1]));
  assign controlled_buffer_37_out = OFF_INL ? {counter_7_q, W_BUS} : 16'bz;  // Controlled_Buffer controlled_buffer_37
  assign controlled_buffer_37_out = OFF_INH ? {W_BUS, counter_7_q_2} : 16'bz;  // Controlled_Buffer controlled_buffer_38
  or or_18 (or_18_out, OFF_INH, OFF_INL);
  assign W_BUS = OFF_OUTH ? counter_7_q_2 : 8'bz;  // Controlled_Buffer controlled_buffer_39
  assign W_BUS = OFF_OUTL ? counter_7_q : 8'bz;  // Controlled_Buffer controlled_buffer_40
  LED D0_15 (.in(counter_7_q_2[0]));
  Counter #(.max('hffff), .width(16)) counter_7 (
    .load(or_18_out), .D(controlled_buffer_37_out), .count(1'b0), .Q({counter_7_q, counter_7_q_2}),
    .up(1'b0), .clk(CLK), .clr(RESET));  // open: carry

  // Notes on the sheet:
  //   ADDRESS REGISTER
  //   ADDRESS BUS
  //   DATA BUS
  //   contents of rom_1 (hex, n*v repeats v):
  //   8 10 a 9 21 a 20 80 9 2 80 9
  //   JUMP LOGIC
  //   32K ROM
  //   PROGRAM COUNTER
  //   32K RAM
  //   contents of _4x28C16 (hex, n*v repeats v):
  //   aaf9 4000 6*3000 aaf9 7*3000 aaf9 800aaf2 800aaf3 20000800 4*3000 aaf9 800aaf2 800aaf3 20017800
  //   4*3000 aaf9 800aaf2 800aaf3 20020800 4*3000 aaf9 5000 52fe 52ff 80052f2 80002f3 20000800 3000 aaf9
  //   1000 6*3000 aaf9 2000 6*3000 aaf9 aafa 4000aaf0 5*3000 aaf9 aafa 40200000 5*3000 aaf9 7*ffffffff
  //   aaf9 7*ffffffff aaf9 7*ffffffff aaf9 7*ffffffff aaf9 7*ffffffff aaf9 7*ffffffff aaf9 7*ffffffff aaf9
  //   7*ffffffff aaf9 7*ffffffff aaf9 7*ffffffff aaf9 7*ffffffff aaf9 7*ffffffff aaf9 7*ffffffff aaf9
  //   7*ffffffff aaf9 7*ffffffff aaf9 7*ffffffff aaf9 7*ffffffff aaf9 7*ffffffff aaf9 7*ffffffff aaf9
  //   7*ffffffff aaf9 7*ffffffff aaf9 7*ffffffff aaf9 7*ffffffff aaf9 7*ffffffff aaf9 7*ffffffff aaf9
  //   7*ffffffff aaf9 7*ffffffff aaf9 7*ffffffff aaf9 7*ffffffff aaf9 7*ffffffff aaf9 7*ffffffff aaf9
  //   7*ffffffff aaf9 7*ffffffff aaf9 7*ffffffff aaf9 7*ffffffff aaf9 7*ffffffff aaf9 7*ffffffff aaf9
  //   7*ffffffff aaf9 7*ffffffff aaf9 7*ffffffff aaf9 7*ffffffff aaf9 7*ffffffff aaf9 7*ffffffff aaf9
  //   7*ffffffff aaf9 7*ffffffff aaf9 7*ffffffff aaf9 7*ffffffff aaf9 7*ffffffff aaf9 7*ffffffff aaf9
  //   7*ffffffff aaf9 7*ffffffff aaf9 7*ffffffff aaf9 7*ffffffff aaf9 7*ffffffff aaf9 7*ffffffff aaf9
  //   7*ffffffff aaf9 7*ffffffff aaf9 7*ffffffff aaf9 7*ffffffff aaf9 7*ffffffff aaf9 7*ffffffff aaf9
  //   7*ffffffff aaf9 7*ffffffff aaf9 7*ffffffff aaf9 7*ffffffff aaf9 7*ffffffff aaf9 7*ffffffff aaf9
  //   7*ffffffff aaf9 7*ffffffff aaf9 7*ffffffff aaf9 7*ffffffff aaf9 7*ffffffff aaf9 7*ffffffff aaf9
  //   7*ffffffff aaf9 7*ffffffff aaf9 7*ffffffff aaf9 7*ffffffff aaf9 7*ffffffff aaf9 7*ffffffff aaf9
  //   7*ffffffff aaf9 7*ffffffff aaf9 7*ffffffff aaf9 7*ffffffff aaf9 7*ffffffff aaf9 7*ffffffff aaf9
  //   7*ffffffff aaf9 7*ffffffff aaf9 7*ffffffff aaf9 7*ffffffff aaf9 7*ffffffff aaf9 7*ffffffff aaf9
  //   7*ffffffff aaf9 7*ffffffff aaf9 7*ffffffff aaf9 7*ffffffff aaf9 7*ffffffff aaf9 7*ffffffff aaf9
  //   7*ffffffff aaf9 7*ffffffff aaf9 7*ffffffff aaf9 7*ffffffff aaf9 7*ffffffff aaf9 7*ffffffff aaf9
  //   7*ffffffff aaf9 7*ffffffff aaf9 7*ffffffff aaf9 7*ffffffff aaf9 7*ffffffff aaf9 7*ffffffff aaf9
  //   7*ffffffff aaf9 7*ffffffff aaf9 7*ffffffff aaf9 7*ffffffff aaf9 7*ffffffff aaf9 7*ffffffff aaf9
  //   800aaf2 800aaf3 62c7 62b7 62d7 62e7 300 aaf9 5000 80052f2 80052f3 52fd 52f4 52f3 52f2 aaf9 6287 6217
  //   6227 6237 6247 6277 62c7 aaf9 7*ffffffff aaf9 7*ffffffff aaf9 7*ffffffff aaf9 7*ffffffff aaf9
  //   7*ffffffff aaf9 7*ffffffff aaf9 7*ffffffff aaf9 7*ffffffff aaf9 7*ffffffff aaf9 7*ffffffff aaf9
  //   7*ffffffff aaf9 7*ffffffff aaf9 7*ffffffff aaf9 7*ffffffff aaf9 7*ffffffff aaf9 7*ffffffff aaf9
  //   7*ffffffff aaf9 7*ffffffff aaf9 7*ffffffff aaf9 7*ffffffff aaf9 7*ffffffff aaf9 7*ffffffff aaf9
  //   7*ffffffff aaf9 7*ffffffff aaf9 7*ffffffff aaf9 7*ffffffff aaf9 7*ffffffff aaf9 7*ffffffff aaf9
  //   7*ffffffff aaf9 7*ffffffff aaf9 7*ffffffff aaf9 7*ffffffff aaf9 7*ffffffff aaf9 7*ffffffff aaf9
  //   7*ffffffff aaf9 7*ffffffff aaf9 7*ffffffff aaf9 7*ffffffff aaf9 7*ffffffff aaf9 7*ffffffff aaf9
  //   7*ffffffff aaf9 7*ffffffff aaf9 7*ffffffff aaf9 7*ffffffff aaf9 7*ffffffff aaf9 7*ffffffff aaf9
  //   7*ffffffff aaf9 7*ffffffff aaf9 7*ffffffff aaf9 7*ffffffff aaf9 7*ffffffff aaf9 7*ffffffff aaf9
  //   7*ffffffff aaf9 7*ffffffff aaf9 7*ffffffff aaf9 7*ffffffff aaf9 7*ffffffff aaf9 7*ffffffff aaf9
  //   7*ffffffff aaf9 7*ffffffff aaf9 7*ffffffff aaf9 7*ffffffff aaf9 7*ffffffff aaf9 7*ffffffff aaf9
  //   7*ffffffff aaf9 7*ffffffff aaf9 7*ffffffff aaf9 7*ffffffff aaf9 7*ffffffff aaf9 7*ffffffff aaf9
  //   7*ffffffff aaf9 7*ffffffff aaf9 7*ffffffff aaf9 7*ffffffff aaf9 7*ffffffff aaf9 7*ffffffff aaf9
  //   7*ffffffff aaf9 7*ffffffff aaf9 7*ffffffff aaf9 7*ffffffff aaf9 7*ffffffff aaf9 7*ffffffff aaf9
  //   7*ffffffff aaf9 7*ffffffff aaf9 7*ffffffff aaf9 7*ffffffff aaf9 7*ffffffff aaf9 7*ffffffff aaf9
  //   7*ffffffff aaf9 7*ffffffff aaf9 7*ffffffff aaf9 7*ffffffff aaf9 7*ffffffff aaf9 7*ffffffff aaf9
  //   7*ffffffff aaf9 7*ffffffff aaf9 7*ffffffff aaf9 7*ffffffff aaf9 7*ffffffff aaf9 7*ffffffff aaf9
  //   7*ffffffff aaf9 7*ffffffff aaf9 7*ffffffff aaf9 7*ffffffff aaf9 7*ffffffff aaf9 7*ffffffff aaf9
  //   7*ffffffff aaf9 7*ffffffff aaf9 7*ffffffff aaf9 7*ff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
  //   INSTRUCTION REGISTER
  //   INSTRUCTION REGISTER 2
  //   OP REG
  //   A REG
  //   B REG
  //   C REG
  //   D REG
  //   MICROCODE
  //   INSTRUCTION DECODER ROM (4x2Kx8)
  //   T STATE
  //   contents of rom_2 (hex, n*v repeats v):
  //   compressed eJztmE1u7LoOhOdehZdw3AQYezndUnH/S3giP/EAmQQBzuQN7qT1Y5HFKtJ0oi+d1+v8jPPj53yd
  //   8lM67XWEznitR1/5/MrZOrN+fP3MXMqP9ZNPLZeRs0hPy+Izymd6HR8/PmPmcvleP/nUchk5SwtP
  //   C79ex8crjoXx8bTwtPC08LTwtPB4HTOjmhnVzKjmq2KfuVTOlE8tz0XOImktCy2M9bMslBjy4rt4
  //   KDGUGEqM9bNmSgulhdJCi4eUFiqN0kJpobTQsrCMylZUh2VUllFZRmUZlb1KV8tl5CxS42URiRGJ
  //   sX58/cxcKmfKp5WLzEZiRGJEMo/EiMSIxIjMRyRGJEa8Kn87g5XDL12sKo9fySeHyaacgZPGZrAq
  //   L38rYfHLn/Ky62FXRNYEAyeNzWAVaVfVkcOuKGpqlJeqkhzESpw07IJVxVIVkwNefFcmXhwvXvVZ
  //   1ZODsYkXLy8TRpPqnjDKWjpymGyKehcnjc1gFbwG5SVrK98HYhGxyPebIlbipLEZrEoXkSORI5Gj
  //   rLka8EKORI6y9soOL+TIYGQwMhgZOTIYGe+t9ZtrbAar4E0uL0EsQSxBvQSxBLEEsYR2B6AHEEsQ
  //   S1AvQSxBLEEsgbpBLLH7SHeSpUtWS3WTqt0cqqNk7dYw2RQrcdKwC1bVkap2c7hYlZeq3Rwmm8o+
  //   VbWbg7EZrIJuVl7+9ja6G/1td7jd43aX231udzp63aDbDfrdoOMNet6g6w363qDzDXrfoPuN6n+J
  //   Vl4mjCaMJowmjKp2a+CkYResgoZcXqov5lBeRCzy3bOXLl//fSP++0b8n38j7j/7K8Fk+WWi3lkW
  //   TGY/+vTOQmBytZ8vrKpa96R3rHfUO9tzMWSydNuTsXeufrQ9l2J70jvWO+od4acywGTHXBlicvWj
  //   8vznTxBzTXqn9MmJeqdizsnsw5/eKc85ufpRe14xH3vSO7bPqD2rPas9qz2rPetqP9uzdczWMdvL
  //   eke9sz1bx2zoXJOxd65+tD1L27M6ZnXM6piFzjmZ/WjHrI5ZuvpRe/b27O3Zt87VK/Zk+/H27O3Z
  //   27O3Z9+esxsde9I7O+bZasxWY7YaszM4W43sftvP9vzpmD8dc3VNJuqd7fnTMWe3PfZk7J2rH7Xn
  //   0Z5Hex7tebTnsXXe72BOdsz7HcxJex7b89W1cbUaV9fz1WpcrcbValytxtVqXF0bV6uRpX3sSe/s
  //   mDPPPfE9mf3o0zvbc7o88v378+fM97GGz2DwGiabYiVO2to88v2vVXAk3jUMNh0vDyux0gKtvrxW
  //   yaqGwkvWNUw2xUqcLLxUsVbBkcK7XoNNx8vDSqwKL/OxVpmfGgov81fDZFOsxMnCy3qoVXCk8D5j
  //   sOl4eViJFXgOnoPn4Dl4Dp6D5+A5eA6eg+fgOXgOnoPn4HnhTfSc6DnRc6LnRM+JnhM9J3pO9Jzo
  //   OdFzoudEz4meEz0negp+gp/gJ/gJfoKf4Cf4CX6Cn+An+Al+gp/gJ/iJ+hT1KepT1KeoT1Gfoj5F
  //   fYr6FPUp6lPUp6hPUZ+iPkV9Gnoaehp6Gnoaehp6Gnoaehp6Gnoaehp6Gnoaehp6GnoG/AJ+Ab+A
  //   X8Av4BfwC/gF/AJ+Ab+AX8Av4BfwC/gF/AJ+Ab+AX8Av4BfwC/gF/AJ+Ab+AX8Av4Bfwi83vDd4b
  //   vDd4b/De4L3Be4P3Bu8N3hu8N3hv8N7gvcF7g/cuvIGeAz0Heg70HOg50HOg50DPgZ4DPQd6DvQc
  //   6DnQc6DnQE+nvzj9xekvTn9x+ovTX5z+4vQXp784/cXpL05/cfqL01+c/uL0lwd+D/we+D3we+D3
  //   wO+B3wO/B34P/B74PfB74PfA74HfAz/BT/AT/AQ/wU/wE/wEP8FP8BP8BD/BT/AT/AQ/3eDd4N3g
  //   3eDd4N3g3eDd4N3g3eDd4N3g3eDd4N3g3YWX37/1Xc2f9Z3NYX0da/AaJptiJU5afjfre5xD2dX3
  //   ugavYbIpVuJk2dVfCDmUXf0FUYPXMNkUK3ESO8fOsXPsHDvHzrFz7LzsJnFO4pzEOYlzEuckzkmc
  //   kzgFnsATeAJP4Ak8gSfwhJ5CT6Gn0FPoKfQUego9jTiNOI04jTiNOI04jTiz8x4//A94/vA/4PHt
  //   v77z1//1/ctd4O9u/85vt3/HD/d95w/3fce3G77z1zd8/3Cn98tbvPPbLd4/3JX98nbs/HY7dvxw
  //   H3b+cB92fLsBO399A/YPd16/vOVi4CR26Cn0FHoKPYWe0r6vwg49jTiNOI04jTiNOI047bVvutLO
  //   yZ+TPyd/Tv6c/Dn5c/Ln5M/Jn5M/J39O/pz8Oflz8ufkz8mfkz8nf07+nPw5+XPy5+TP910c+fO/
  //   93HYcSe3b+X2vRz5c/Ln5M/Jn5M/J39O/pz8Oflz8ufkz8mfkz9X3wFyCwge+XPy5+TPyZ+TPyd/
  //   Tv6c/Dn5c/Ln5M/Jn5M/J39O/pz8eeXvfzQ8BsM=
  //   ALU REG
  //   DISPLAY DECODER ROM (4x1Kx8)
  //   FLAGS
  //   FRAME POINTER
  //   STACK POINTER
  //   OFFSET REGISTER
endmodule
